# Fritzing sketch Sketch (saved by Fritzing 0.9.3b)
breadboards: 1

parts:
  Arduino_UNO = Arduino Uno (Rev3)
  Node_MCU = NodeMCU V3.0
  DHT11 = DHT11 Humitidy and Temperature Sensor
  R2 = Resistor [tolerance=±5% resistance=10k package="0603 [SMD]"]
  R3 = Resistor [tolerance=±5% resistance=10k package="0603 [SMD]"]
  LDR = Photocell (LDR) [package=THT]
  LCD_with_I2C = LCD1602-I2C
  Part4 = FC-28 Soil Hygrometer Module - Probe
  Soil_Moisture_Sensor = FC-28 Soil Hygrometer Module

nets:
  N1: Arduino_UNO.A0, R2.Pin_1, LDR.pin_0
  N2: Arduino_UNO.A1, Soil_Moisture_Sensor.AO
  N3: Arduino_UNO.A4/SDA, LCD_with_I2C.SDA
  N4: Arduino_UNO.A5/SCL, LCD_with_I2C.SCL
  N5: Arduino_UNO.D0/RX, Node_MCU.RX
  N6: Arduino_UNO.D1/TX, Node_MCU.TX
  N7: Arduino_UNO.D7, DHT11.DATA, R3.Pin_0
  N8: Arduino_UNO.3V3, LDR.pin_1
  VCC: Arduino_UNO.5V, DHT11.VDD, R3.Pin_1, LCD_with_I2C.VCC, Soil_Moisture_Sensor.VCC
  GND: Arduino_UNO.GND, DHT11.GND, R2.Pin_0, LCD_with_I2C.GND, Soil_Moisture_Sensor.GND
  N9: Part4.POS, Soil_Moisture_Sensor.POS
  N10: Part4.NEG, Soil_Moisture_Sensor.NEG

custom parts:
  NodeMCU V3.0: ESP8266 based NodeMCU
  DHT11 Humitidy and Temperature Sensor: DHT11 Humidity and Temperature Sensor
  LCD1602-I2C: A standard character display, usually with 2x16 characters. Comes in many colors with LCM1602 IIC attached.
  FC-28 Soil Hygrometer Module - Probe: The FC-28 is a soil hygrometer module that uses the Texas Instruments LM393 comparator chip to provide an analog measurement of soil humidity.
  FC-28 Soil Hygrometer Module: The FC-28 is a soil hygrometer module that uses the Texas Instruments LM393 comparator chip to provide an analog measurement of soil humidity. The digital output is high when soil moisture is over a certain threshold, as determined by adjusting the potentiometer.

// code stored in the sketch: Node.ino
#include <ESP8266WiFi.h>
#include <WiFiClient.h>
#include <ESP8266WebServer.h>
#include <ESP8266HTTPClient.h>

/* Set these to your desired credentials. */
const char *ssid = "Peace squ";  //ENTER YOUR WIFI SETTINGS
const char *password = "dhaka1207";
const char *host = "192.168.43.161";

String str;
void setup() {
  Serial.begin(9600);
  // Wifi Setup
  WifiSetup();
}
void loop() {
  receiver();
  sendToServer(str);
  delay(2000);
}

void WifiSetup() {
  WiFi.begin(ssid, password);

  while (WiFi.status() != WL_CONNECTED) {
    delay(1000);
    Serial.println("Connecting to WiFi..");
  }

  Serial.println("Connected to the WiFi network");
  Serial.println(ssid);
  Serial.print("IP address: ");
  Serial.println(WiFi.localIP());  //IP address assigned to your ESP
}

void sendToServer(String post) {
  if (WiFi.status() == WL_CONNECTED) { //Check WiFi connection status
    HTTPClient http;    //Declare object of class HTTPClient
    //http.begin("http://"+String(host)+"/Api/eco-friend/insert.php");      //Specify request destination
//    http.begin("http://" + String(host) + "/Api/eco-friend/insert-csv.php");
    http.begin("http://api-tanveer.herokuapp.com/eco-friend/insert-csv.php");
    http.addHeader("Content-Type", "text/plain"); //Specify content-type header

    int httpCode = http.POST(str); //Send the request
    String payload = http.getString();                  //Get the response payload

    Serial.println(httpCode);   //Print HTTP return code
    Serial.println(payload);    //Print request response payload

    http.end();  //Close connection

  } else {

    Serial.println("Error in WiFi connection");

  }

}
void receiver() {
  
  str = Serial.readString();
  Serial.println(str);
  delay(1000);
}

// code stored in the sketch: UNO.ino
// Libraries
#include <SoftwareSerial.h>
#include <LiquidCrystal_I2C.h>
LiquidCrystal_I2C lcd(0x3F, 16, 2);

#include <dht.h>
dht DHT;
// Pin setup

#define DHT11_PIN 7                                      // DHT
const int ldrPin = A0;                                  // LDR
int moistPin = A1;                                      // Soil Moisture

int tmp, lux, moist, hmd = 0;                           // Initial variables for sensor
String light = "";

/* Serial lists
    UNO Serial 115200
    Node Serial 9600
*/

void setup() {
  // Pinsetup
  pinMode(ldrPin, INPUT);
  // DHT & Soil moisture sensore doesn't need pin setup

  // Own Serial
  Serial.begin(9600);

  // Boot msg
  lcd.begin();
  lcd.backlight();
  Serial.print("Device Booting");
  lcd.print("Device Booting");

  for (int i = 0; i < 5; i++) {
    Serial.print(".");
    lcd.print(".");
    delay(500);
  }
  lcd.clear();
  Serial.println();
}

void loop() {
  Light();
  Temp();
  Moist();
  transmitter();
  Print();
}

void Light() {
  lux = analogRead(ldrPin); // read the value from the sensor
  if(lux > 300){
    light = "HIGH";
  } else {
    light = "LOW";
  }
  return;
}

void Temp() {
  int chk = DHT.read11(DHT11_PIN);
  tmp = DHT.temperature;
  hmd = DHT.humidity;
  return;
}

void Moist() {
  moist = analogRead(moistPin);
  //   moist = map(moist,550,0,0,100);
  moist = (100 - ((moist / 1023.00) * 100));
}

void transmitter() {
  String data = "h=" + String(hmd) + "&m=" + String(moist) + "&l=" + String(light) + "&t=" + String(tmp) + "\n";
  Serial.println(data);
}
void Print() {
  lcd.clear();
  lcd.setCursor(0, 0);
  lcd.print("Eco Friend");
  lcd.setCursor(0, 1);
  lcd.print("Temperature:" + String(tmp) + ((char)223)+"c");
  delay(1000);
  lcd.clear();
  lcd.setCursor(0, 0);
  lcd.print("Eco Friend");
  lcd.setCursor(0,1);
  lcd.print("Light: " + String(lux)+"("+light+")");
  delay(1000);
  lcd.clear();
  lcd.setCursor(0, 0);
  lcd.print("Eco Friend");
  lcd.setCursor(0, 1);
  lcd.print("Humidity: " + String(hmd) + "%");
  delay(1000);
  lcd.clear();
  lcd.setCursor(0, 0);
  lcd.print("Eco Friend");
  lcd.setCursor(0,1);
  lcd.print("Soil Moist: " + String(moist)+"%");
  delay(1000);
}
